# Fritzing sketch 20140618-lcd (saved by Fritzing 0.9.0b)
circuit board: 8cm x 3.6cm
breadboards: 1

parts:
  J3 = male pin header, 16 pins [form="♂ (male)"]
  J4 = double row male pin header, 26 pins [form="♂ (male)"]
  R1 = Trimmer Potentiometer [maximum_resistance=10kΩ package=THT]
  J1 = male pin header, 8 pins [form="♂ (male)"]
  J5 = male pin header, 8 pins [form="♂ (male)"]

nets:
  N1: J3.pin1, J3.pin12, J3.pin16, J4.pin24, R1.leg1, J1.pin7, J5.pin7
  N2: J3.pin2, J3.pin15, J4.pin26, R1.leg2, J1.pin8, J5.pin8
  N3: J3.pin3, J4.pin8, J1.pin6, J5.pin6
  N4: J3.pin4, J4.pin7, J1.pin5, J5.pin5
  N5: J3.pin5, J4.pin21, J1.pin4, J5.pin4
  N6: J3.pin6, J4.pin19, J1.pin3, J5.pin3
  N7: J3.pin11, J4.pin18, J5.pin2
  N8: J3.pin13, J4.pin16, J1.pin1, J5.pin1
  N9: J3.pin14, R1.wiper
  N10: J4.pin6, J1.pin2

notes:
  2014-06-18 // postspectacular.com
  DevArt CodeFactory LCD splitter
  LCD
  GPIO
  OUT
  IN
  Made with Fritzing.org
